# Fritzing sketch assignment3_template1new (saved by Fritzing 0.9.4)
breadboards: 1

parts:
  Part1 = Arduino Nano (Rev3.0) (ICSP)
  R1 = Resistor [tolerance=±5% resistance=220 package=THT]
  R2 = Resistor [tolerance=±5% resistance=330 package=THT]
  R3 = Resistor [tolerance=±5% resistance=470 package=THT]
  R4 = Resistor [tolerance=±5% resistance=220 package=THT]
  R5 = Resistor [tolerance=±5% resistance=330 package=THT]
  R6 = Resistor [tolerance=±5% resistance=470 package=THT]
  R7 = Resistor [tolerance=±5% resistance=220 package=THT]
  R8 = Resistor [tolerance=±5% resistance=330 package=THT]
  R9 = Resistor [tolerance=±5% resistance=470 package=THT]

nets:
  GND: Part1.GND, R3.Pin_1, R4.Pin_1, R5.Pin_1, R6.Pin_1, R9.Pin_1
  5V: Part1.5V, R1.Pin_0, R4.Pin_0, R5.Pin_0, R6.Pin_0, R7.Pin_0
  N1: Part1.A0, R8.Pin_1, R9.Pin_0
  N2: R1.Pin_1, R2.Pin_0
  N3: R2.Pin_1, R3.Pin_0
  N4: R7.Pin_1, R8.Pin_0

notes:
  V1 = 1.078
  V2 = 1.61
  V3 = 2.30
  I4 = 0.022
  I5 = 0.015
  I6 = 0.010
  Rseries = 1020
  Rparallel = 103.05
  VA0 = 1.078
  analogRead(A0) = ??
