# Fritzing sketch assignment3_template2new (saved by Fritzing 0.9.4)
breadboards: 1

parts:
  LED1 = LED - 5mm [color="Red (633nm)" package="5 mm [THT]"]
  Part1 = Arduino Nano (Rev3.0) (ICSP)
  LED2 = LED - 5mm [color="Yellow (595nm)" package="5 mm [THT]"]
  LED3 = LED - 5mm [color="Green (560nm)" package="5 mm [THT]"]
  R1 = Resistor [tolerance=±5% resistance=220 package=THT]
  R2 = Resistor [tolerance=±5% resistance=100 package=THT]
  R3 = Resistor [tolerance=±5% resistance=100 package=THT]
  R4 = Resistor [tolerance=±5% resistance=470 package=THT]  # not connected
  R5 = Resistor [tolerance=±5% resistance=470 package=THT]

nets:
  N1: LED1.cathode, R1.Pin_0
  N2: LED1.anode, Part1.D6
  N3: Part1.D3, LED3.anode
  N4: Part1.D5, LED2.anode
  N5: LED2.cathode, R2.Pin_0
  N6: LED3.cathode, R5.Pin_0
  N7: R1.Pin_1, R3.Pin_1
